// Logisim project lab2.circ as structural Verilog: 1 circuit, main circuit main
module main (
  input  S,
  input  A1,
  input  A0,
  input  B1,
  input  B0,
  output Y1,
  output Y0
);

  wire and_1_out, and_2_out, and_3_out, and_4_out, and_5_out, and_6_out, n3_to_8_decoder_74138_1_p4,
       n3_to_8_decoder_74138_1_p5, n3_to_8_decoder_74138_1_p6, n3_to_8_decoder_74138_1_p7,
       n3_to_8_decoder_74138_2_p10, n3_to_8_decoder_74138_2_p11, n3_to_8_decoder_74138_2_p12,
       n3_to_8_decoder_74138_2_p13, n3_to_8_decoder_74138_2_p14, n3_to_8_decoder_74138_2_p15, not_1_out,
       not_2_out, not_3_out, not_4_out, not_5_out, not_6_out, not_7_out, not_8_out, not_9_out, not_10_out,
       not_11_out, not_12_out, not_13_out, or_1_out, or_2_out, or_3_out, or_4_out, or_5_out, or_6_out,
       or_7_out, or_8_out, or_9_out, or_10_out;

  and and_1 (and_1_out, A1, B1);
  and and_2 (and_2_out, A0, B0);
  not not_1 (not_1_out, A1);
  and and_3 (and_3_out, not_1_out, A0);
  not not_2 (not_2_out, A1);
  and and_4 (and_4_out, and_3_out, B1);
  // _3_to_8_decoder__74138 #(.Facing("east")) 3_to_8_decoder_74138_1: pin names not known; wires that end beside it: B0, B1, A0, n3_to_8_decoder_74138_1_p4, n3_to_8_decoder_74138_1_p5, n3_to_8_decoder_74138_1_p6, n3_to_8_decoder_74138_1_p7
  // _3_to_8_decoder__74138 #(.Facing("east")) 3_to_8_decoder_74138_2: pin names not known; wires that end beside it: B0, B1, A0, not_2_out, A1, 1'b0, 1'b0, 1'b0, 1'b0, n3_to_8_decoder_74138_2_p10, n3_to_8_decoder_74138_2_p11, n3_to_8_decoder_74138_2_p12, n3_to_8_decoder_74138_2_p13, n3_to_8_decoder_74138_2_p14, n3_to_8_decoder_74138_2_p15
  and and_5 (and_5_out, A1, not_3_out);
  not not_3 (not_3_out, B1);
  and and_6 (and_6_out, and_5_out, B0);
  not not_4 (not_4_out, n3_to_8_decoder_74138_1_p4);
  not not_5 (not_5_out, n3_to_8_decoder_74138_1_p6);
  or or_1 (or_1_out, and_2_out, or_2_out);
  or or_2 (or_2_out, and_6_out, and_4_out);
  or or_3 (or_3_out, not_4_out, not_5_out);
  not not_6 (not_6_out, n3_to_8_decoder_74138_2_p10);
  or or_4 (or_4_out, not_6_out, not_7_out);
  not not_7 (not_7_out, n3_to_8_decoder_74138_2_p12);
  not not_8 (not_8_out, n3_to_8_decoder_74138_2_p14);
  or or_5 (or_5_out, or_3_out, or_4_out);
  not not_9 (not_9_out, n3_to_8_decoder_74138_1_p5);
  not not_10 (not_10_out, n3_to_8_decoder_74138_1_p7);
  not not_11 (not_11_out, n3_to_8_decoder_74138_2_p11);
  not not_12 (not_12_out, n3_to_8_decoder_74138_2_p13);
  not not_13 (not_13_out, n3_to_8_decoder_74138_2_p15);
  or or_6 (or_6_out, or_5_out, not_8_out);
  or or_7 (or_7_out, not_9_out, not_10_out);
  or or_8 (or_8_out, not_11_out, not_12_out);
  or or_9 (or_9_out, or_7_out, or_8_out);
  or or_10 (or_10_out, or_9_out, not_13_out);
  // _4_to_1_MUX__x2___74153 #(.Facing("east")) 4_to_1_mux_x2_74153_1: pin names not known; wires that end beside it: or_1_out, or_10_out, and_1_out, or_6_out, 1'b0, S, 1'b0, S, Y1, Y0
endmodule
